# Fritzing sketch p-mosfet rpp (saved by Fritzing 0.9.2b)
breadboards: 1

parts:
  LED1 = LED - 5mm [color="Red (633nm)" package="5 mm [THT]"]
  LED2 = LED - 5mm [color="Red (633nm)" package="5 mm [THT]"]
  TSM2311 = MOSFET-PCHANNEL [package=sot23-3]
  R1 = Resistor [tolerance=±5% resistance=220 package=THT]
  VCC1 = Battery

nets:
  N1: LED1.cathode, LED2.anode, R1.Pin_0
  N2: LED1.anode, LED2.cathode, TSM2311.S
  N3: TSM2311.G, R1.Pin_1, VCC1.-
  N4: TSM2311.D, VCC1.+
